# Fritzing sketch rpi_btn_led_servo (saved by Fritzing 0.9.3b)
breadboards: 1

parts:
  Raspberry_Pi_1 = Raspberry Pi 3 [part_number=RPI-3-V1.2]
  S1 = Momentary Switch [package=ksa_sealed_tac_switch]
  R1 = Resistor [tolerance=±5% resistance=220 package="1206 [SMD]"]
  LED1 = LED - 5mm [color="Red (633nm)" package="5 mm [THT]"]
  J1 = Basic Servo  # not connected

nets:
  N1: Raspberry_Pi_1.GND, S1.4
  N2: Raspberry_Pi_1.GIPO15, LED1.anode
  N3: Raspberry_Pi_1.GIPO14, S1.2
  N4: S1.3, R1.Pin_0
  N5: R1.Pin_1, LED1.cathode
